// Digital circuit CircuitoFinal_Coninversores.dig as structural Verilog
module CircuitoFinal_Coninversores (
  input  R,
  input  B,
  input  S,
  input  E,
  output Energia,
  output IBB,
  output IRD,
  output IS,
  output _1_B,
  output _1_S,
  output _1_R
);

  wire nand_1_out, nand_2_out, nand_3_out, nand_4_out, nand_5_out, not_1_out, not_2_out, not_3_out;

  not not_1 (not_1_out, R);
  not not_2 (not_2_out, S);
  not not_3 (not_3_out, E);
  nand nand_1 (nand_1_out, B, not_3_out);
  nand nand_2 (nand_2_out, not_3_out, S);
  nand nand_3 (nand_3_out, not_3_out, R);
  nand nand_4 (nand_4_out, B, not_1_out, not_2_out);
  nand nand_5 (nand_5_out, not_1_out, S);
  not not_4 (_1_B, nand_4_out);
  not not_5 (_1_S, nand_5_out);
  nand nand_6 (Energia, nand_1_out, nand_2_out, nand_3_out);

  assign _1_R = R;
  assign IBB = B;
  assign IRD = R;
  assign IS = S;
endmodule
