// Digital circuit Final_NAND.dig as structural Verilog
module Final_NAND (
  input  R,
  input  B,
  input  S,
  input  E,
  output Energia,
  output IBB,
  output IRD,
  output IS,
  output _1_B,
  output _1_S,
  output _1_R
);

  wire nand_1_out, nand_2_out, nand_3_out, nand_4_out, nand_5_out, nand_7_out, nand_8_out, nand_9_out,
       nand_10_out, nand_11_out, nand_12_out, nand_13_out, nand_14_out, nand_15_out, nor_1_out;

  nand nand_1 (nand_1_out, R, R);
  nor nor_1 (nor_1_out, S, B);
  nand nand_2 (nand_2_out, E, E);
  nand nand_3 (nand_3_out, B, nand_2_out);
  nand nand_4 (nand_4_out, nand_2_out, R);
  nand nand_5 (nand_5_out, nand_2_out, S);
  nand nand_6 (Energia, nand_3_out, nand_5_out, nand_4_out);
  nand nand_7 (nand_7_out, nor_1_out, nor_1_out);
  nand nand_8 (nand_8_out, S, S);
  nand nand_9 (nand_9_out, nand_7_out, nand_1_out);
  nand nand_10 (nand_10_out, nand_8_out, B);
  nand nand_11 (nand_11_out, nand_9_out, nand_9_out);
  nand nand_12 (nand_12_out, nand_10_out, nand_10_out);
  nand nand_13 (nand_13_out, nand_12_out, nand_12_out);
  nand nand_14 (nand_14_out, nand_12_out, nand_11_out);
  nand nand_15 (nand_15_out, nand_13_out, nand_11_out);
  nand nand_16 (_1_B, nand_14_out, nand_14_out);
  nand nand_17 (_1_S, nand_15_out, nand_15_out);

  assign _1_R = R;
  assign IBB = B;
  assign IRD = R;
  assign IS = S;
endmodule
