// Digital circuit Final_Simplificado.dig as structural Verilog
module Final_Simplificado (
  input  R,
  input  B,
  input  S,
  input  E,
  output Energia,
  output IBB,
  output IRD,
  output IS,
  output _0_R___1_B
);

  wire and_1_out, and_2_out, not_1_out;

  not not_1 (not_1_out, R);
  and and_1 (and_1_out, B, E);
  and and_2 (and_2_out, E, R);
  and and_3 (IS, E, S);
  and and_4 (_0_R___1_B, B, not_1_out);
  or or_1 (Energia, and_1_out, and_2_out);

  assign IBB = B;
  assign IRD = R;
endmodule
