// Digital circuit Test1_Ladder_CL.dig as structural Verilog
module Test1_Ladder_CL (
  input  R,
  input  B,
  input  S,
  input  E
);

  wire and_1_out, and_2_out, and_3_out, and_4_out, multiplexer_1_out, nand_1_out, nand_2_out, not_1_out,
       or_1_out, or_2_out;

  nand nand_1 (nand_1_out, R, B);
  or or_1 (or_1_out, R, B);
  nand nand_2 (nand_2_out, or_1_out, nand_1_out);
  not not_1 (not_1_out, R);
  and and_1 (and_1_out, not_1_out, B);
  Multiplexer multiplexer_1 (.sel(nand_2_out), .in_0(R), .in_1(B), .out(multiplexer_1_out));
  and and_2 (and_2_out, E, S);
  and and_3 (and_3_out, B, E);
  and and_4 (and_4_out, multiplexer_1_out, E);
  or or_2 (or_2_out, and_4_out, and_3_out);
  LED _0_R___1_B (.in(and_1_out));
  LED IRD (.in(R));
  LED IBB (.in(B));
  LED Energia (.in(or_2_out));
  LED IS (.in(and_2_out));
endmodule
